// Logisim project DDCA project circuit 2.circ as structural Verilog: 1 circuit, main circuit main
module main (
  input  in_1,
  input  in_2,
  input  in_3,
  input  in_4,
  output out_5
);

  wire not_1_out;

  not not_1 (not_1_out, in_2);
  and and_1 (out_5, in_1, not_1_out, in_3, in_4);
endmodule
