// Logisim project ProjLogisim - 2.circ as structural Verilog: 1 circuit, main circuit main
module main (
  input  CRT,
  input  A0,
  input  B0,
  input  A1,
  input  B1,
  input  A2,
  input  B2,
  input  A3,
  input  B3,
  output S0,
  output S1,
  output S2,
  output S3,
  output C4
);

  wire adder_1_cout, adder_2_cout, adder_3_cout, adder_4_cout, xor_1_out, xor_2_out, xor_3_out, xor_4_out;

  xor xor_1 (xor_1_out, B0, CRT);
  xor xor_2 (xor_2_out, B1, CRT);
  xor xor_3 (xor_3_out, CRT, B2);
  xor xor_4 (xor_4_out, B3, CRT);
  Adder #(.width(1)) adder_1 (.a(A0), .b(xor_1_out), .out(S0), .cin(CRT), .cout(adder_1_cout));
  Adder #(.width(1)) adder_2 (.a(A1), .b(xor_2_out), .out(S1), .cin(adder_1_cout), .cout(adder_2_cout));
  Adder #(.width(1)) adder_3 (.a(A2), .b(xor_3_out), .out(S2), .cin(adder_2_cout), .cout(adder_3_cout));
  Adder #(.width(1)) adder_4 (.a(A3), .b(xor_4_out), .out(S3), .cin(adder_3_cout), .cout(adder_4_cout));

  // Notes on the sheet:
  //   C0
  //   C1
  //   C2
  //   C3
endmodule
